// Logisim project Oblig1.circ as structural Verilog: 2 circuits, main circuit main
module main (
  input  [2:0] in_1
);

  wire decoder_1_a, decoder_1_b, decoder_1_c, decoder_1_d, decoder_1_e, decoder_1_f, decoder_1_g;

  Decoder decoder_1 (
    .x0(in_1[0]), .x1(in_1[1]), .x2(in_1[2]), .a(decoder_1_a), .b(decoder_1_b), .c(decoder_1_c),
    .d(decoder_1_d), .e(decoder_1_e), .f(decoder_1_f), .g(decoder_1_g));
  _7_Segment_Display u_7_segment_display_1 (
    .g(decoder_1_g), .f(decoder_1_f), .a(decoder_1_a), .b(decoder_1_b), .e(decoder_1_e), .d(decoder_1_d),
    .c(decoder_1_c), .dp(1'b0));
endmodule

module Decoder (
  input  x0,
  input  x1,
  input  x2,
  output a,
  output b,
  output c,
  output d,
  output e,
  output f,
  output g
);

  wire _0_out, _1_out, _2_out, _3_out, _4_out, _5_out, _6_out, notX0, notX1, notX2;

  not not_1 (notX0, x0);
  not not_2 (notX1, x1);
  not not_3 (notX2, x2);
  and _1 (_1_out, x0, notX1, notX2);
  and _2 (_2_out, x1, notX0, notX2);
  and _3 (_3_out, x0, x1, notX2);
  and _4 (_4_out, x2, notX0, notX1);
  and _5 (_5_out, x0, x2, notX1);
  and _6 (_6_out, x1, x2, notX0);
  and _0 (_0_out, notX0, notX1, notX2);
  or or_1 (a, _2_out, _3_out, _5_out, _6_out, _0_out);
  or or_2 (b, _1_out, _2_out, _3_out, _4_out, _0_out);
  or or_3 (c, _1_out, _3_out, _4_out, _5_out, _6_out, _0_out);
  or or_4 (d, _2_out, _3_out, _5_out, _6_out, _0_out);
  or or_5 (e, _2_out, _6_out, _0_out);
  or or_6 (f, _4_out, _5_out, _6_out, _0_out);
  or or_7 (g, _2_out, _3_out, _4_out, _5_out, _6_out);
endmodule
