// Logisim project Oblig2.circ as structural Verilog: 4 circuits, main circuit main
module main (
);

  wire _1_out, _2_out, _3_out, _4_out, _5_out, _6_out, _7_out, clock_1_out, encoder_1_x0, encoder_1_x1,
       encoder_1_x2, statesetter_1_unlock;

  Button _7 (.out(_7_out));
  Button _6 (.out(_6_out));
  Button _3 (.out(_3_out));
  Button _4 (.out(_4_out));
  Button _1 (.out(_1_out));
  Button _5 (.out(_5_out));
  Button _2 (.out(_2_out));
  encoder encoder_1 (
    ._7(_7_out), ._6(_6_out), ._5(_5_out), ._4(_4_out), ._3(_3_out), ._2(_2_out), ._1(_1_out),
    .x2(encoder_1_x2), .x1(encoder_1_x1), .x0(encoder_1_x0));
  Clock clock_1 (.out(clock_1_out));
  Statesetter statesetter_1 (
    .clk(clock_1_out), .x2(encoder_1_x2), .x1(encoder_1_x1), .x0(encoder_1_x0), .unlock(statesetter_1_unlock));
  LED led_1 (.in(statesetter_1_unlock));
endmodule

module Decoder (
  input  Q1,
  input  Q0,
  input  x2,
  input  x1,
  input  x0,
  output D1,
  output D0,
  output Out
);

  wire and_1_out, and_2_out, and_3_out, and_4_out, and_5_out, and_6_out, and_7_out, and_8_out, and_9_out,
       not_1_out, not_2_out, not_3_out, not_4_out, not_5_out, not_6_out, not_7_out, not_8_out, not_9_out,
       not_10_out, not_11_out, not_12_out, not_13_out, not_14_out, not_15_out, not_16_out, not_17_out,
       not_18_out, not_19_out;

  not not_1 (not_1_out, Q1);
  not not_2 (not_2_out, x2);
  not not_3 (not_3_out, x0);
  not not_4 (not_4_out, Q0);
  not not_5 (not_5_out, x0);
  not not_6 (not_6_out, x0);
  not not_7 (not_7_out, x2);
  not not_8 (not_8_out, x1);
  not not_9 (not_9_out, x0);
  not not_10 (not_10_out, Q1);
  not not_11 (not_11_out, x1);
  not not_12 (not_12_out, x0);
  not not_13 (not_13_out, x2);
  not not_14 (not_14_out, x1);
  not not_15 (not_15_out, x0);
  not not_16 (not_16_out, x0);
  not not_17 (not_17_out, x2);
  not not_18 (not_18_out, x1);
  not not_19 (not_19_out, x0);
  and and_1 (and_1_out, not_1_out, Q0, not_2_out, x1, not_3_out);
  and and_2 (and_2_out, Q1, not_4_out, x1, not_5_out);
  and and_3 (and_3_out, Q1, x2, x1, not_6_out);
  and and_4 (and_4_out, Q1, Q0, not_7_out, not_8_out, not_9_out);
  and and_5 (and_5_out, not_10_out, x2, not_11_out, x0);
  and and_6 (and_6_out, Q1, x2, x1, not_12_out);
  and and_7 (and_7_out, Q1, Q0, not_13_out, not_14_out, not_15_out);
  and and_8 (and_8_out, Q1, x2, x1, not_16_out);
  and and_9 (and_9_out, Q1, Q0, not_17_out, not_18_out, not_19_out);
  or or_1 (D1, and_1_out, and_2_out, and_3_out, and_4_out);
  or or_2 (D0, and_5_out, and_6_out, and_7_out);
  or or_3 (Out, and_8_out, and_9_out);
endmodule

module Statesetter (
  input  clk,
  input  x2,
  input  x1,
  input  x0,
  output unlock
);

  wire d0, d1, enable, Q0, Q1;

  D_Flip_Flop d_ff_1 (.clk(clk), .D(d1), .Q(Q1), .preset(1'b0), .en(enable), .reset(1'b0));  // open: Qn
  D_Flip_Flop d_ff_2 (.clk(clk), .D(d0), .Q(Q0), .preset(1'b0), .en(enable), .reset(1'b0));  // open: Qn
  or or_1 (enable, x2, x1, x0);
  Decoder decoder_1 (.Q1(Q1), .Q0(Q0), .x2(x2), .x1(x1), .x0(x0), .D1(d1), .D0(d0), .Out(unlock));
endmodule

module encoder (
  input  _7,
  input  _6,
  input  _5,
  input  _4,
  input  _3,
  input  _2,
  input  _1,
  output x2,
  output x1,
  output x0
);

  wire and_1_out, and_2_out, and_3_out, and_4_out, and_5_out, and_6_out, and_7_out, and_8_out, and_9_out,
       and_10_out, and_11_out, and_12_out, not_1_out, not_2_out, not_3_out, not_4_out, not_5_out, not_6_out,
       not_7_out, not_8_out, not_9_out, not_10_out, not_11_out, not_12_out, not_13_out, not_14_out,
       not_15_out, not_16_out, not_17_out, not_18_out, not_19_out, not_20_out, not_21_out, not_22_out,
       not_23_out, not_24_out, not_25_out, not_26_out, not_27_out, not_28_out, not_29_out, not_30_out,
       not_31_out, not_32_out, not_33_out, not_34_out, not_35_out, not_36_out, not_37_out, not_38_out,
       not_39_out, not_40_out, not_41_out, not_42_out, not_43_out, not_44_out, not_45_out, not_46_out,
       not_47_out, not_48_out, not_49_out, not_50_out, not_51_out, not_52_out, not_53_out, not_54_out,
       not_55_out, not_56_out, not_57_out, not_58_out, not_59_out, not_60_out, not_61_out, not_62_out,
       not_63_out, not_64_out, not_65_out, not_66_out, not_67_out, not_68_out, not_69_out, not_70_out,
       not_71_out, not_72_out;

  not not_1 (not_1_out, _7);
  not not_2 (not_2_out, _6);
  not not_3 (not_3_out, _5);
  not not_4 (not_4_out, _3);
  not not_5 (not_5_out, _2);
  not not_6 (not_6_out, _1);
  not not_7 (not_7_out, _7);
  not not_8 (not_8_out, _6);
  not not_9 (not_9_out, _4);
  not not_10 (not_10_out, _3);
  not not_11 (not_11_out, _2);
  not not_12 (not_12_out, _1);
  not not_13 (not_13_out, _7);
  not not_14 (not_14_out, _5);
  not not_15 (not_15_out, _4);
  not not_16 (not_16_out, _3);
  not not_17 (not_17_out, _2);
  not not_18 (not_18_out, _1);
  not not_19 (not_19_out, _6);
  not not_20 (not_20_out, _5);
  not not_21 (not_21_out, _4);
  not not_22 (not_22_out, _3);
  not not_23 (not_23_out, _2);
  not not_24 (not_24_out, _1);
  not not_25 (not_25_out, _7);
  not not_26 (not_26_out, _6);
  not not_27 (not_27_out, _5);
  not not_28 (not_28_out, _4);
  not not_29 (not_29_out, _3);
  not not_30 (not_30_out, _1);
  not not_31 (not_31_out, _7);
  not not_32 (not_32_out, _6);
  not not_33 (not_33_out, _5);
  not not_34 (not_34_out, _4);
  not not_35 (not_35_out, _2);
  not not_36 (not_36_out, _1);
  not not_37 (not_37_out, _7);
  not not_38 (not_38_out, _5);
  not not_39 (not_39_out, _4);
  not not_40 (not_40_out, _3);
  not not_41 (not_41_out, _2);
  not not_42 (not_42_out, _1);
  not not_43 (not_43_out, _6);
  not not_44 (not_44_out, _5);
  not not_45 (not_45_out, _4);
  not not_46 (not_46_out, _3);
  not not_47 (not_47_out, _2);
  not not_48 (not_48_out, _1);
  not not_49 (not_49_out, _7);
  not not_50 (not_50_out, _6);
  not not_51 (not_51_out, _5);
  not not_52 (not_52_out, _4);
  not not_53 (not_53_out, _3);
  not not_54 (not_54_out, _2);
  not not_55 (not_55_out, _7);
  not not_56 (not_56_out, _6);
  not not_57 (not_57_out, _5);
  not not_58 (not_58_out, _4);
  not not_59 (not_59_out, _2);
  not not_60 (not_60_out, _1);
  not not_61 (not_61_out, _7);
  not not_62 (not_62_out, _6);
  not not_63 (not_63_out, _4);
  not not_64 (not_64_out, _3);
  not not_65 (not_65_out, _2);
  not not_66 (not_66_out, _1);
  not not_67 (not_67_out, _6);
  not not_68 (not_68_out, _5);
  not not_69 (not_69_out, _4);
  not not_70 (not_70_out, _3);
  not not_71 (not_71_out, _2);
  not not_72 (not_72_out, _1);
  and and_1 (and_1_out, not_1_out, not_2_out, not_3_out, _4, not_4_out, not_5_out, not_6_out);
  and and_2 (and_2_out, not_7_out, not_8_out, _5, not_9_out, not_10_out, not_11_out, not_12_out);
  and and_3 (and_3_out, not_13_out, _6, not_14_out, not_15_out, not_16_out, not_17_out, not_18_out);
  and and_4 (and_4_out, _7, not_19_out, not_20_out, not_21_out, not_22_out, not_23_out, not_24_out);
  and and_5 (and_5_out, not_25_out, not_26_out, not_27_out, not_28_out, not_29_out, _2, not_30_out);
  and and_6 (and_6_out, not_31_out, not_32_out, not_33_out, not_34_out, _3, not_35_out, not_36_out);
  and and_7 (and_7_out, not_37_out, _6, not_38_out, not_39_out, not_40_out, not_41_out, not_42_out);
  and and_8 (and_8_out, _7, not_43_out, not_44_out, not_45_out, not_46_out, not_47_out, not_48_out);
  and and_9 (and_9_out, not_49_out, not_50_out, not_51_out, not_52_out, not_53_out, not_54_out, _1);
  and and_10 (and_10_out, not_55_out, not_56_out, not_57_out, not_58_out, _3, not_59_out, not_60_out);
  and and_11 (and_11_out, not_61_out, not_62_out, _5, not_63_out, not_64_out, not_65_out, not_66_out);
  and and_12 (and_12_out, _7, not_67_out, not_68_out, not_69_out, not_70_out, not_71_out, not_72_out);
  or or_1 (x2, and_1_out, and_2_out, and_3_out, and_4_out);
  or or_2 (x1, and_5_out, and_6_out, and_7_out, and_8_out);
  or or_3 (x0, and_9_out, and_10_out, and_11_out, and_12_out);
endmodule
