// Logisim project Oblig2a.circ as structural Verilog
module counter (
  input  carry_in,
  input  [3:0] num0,
  input  clock,
  output carry_out
);

  wire and_1_out;
  wire [3:0] adder_1_out, register_1_q;

  Register #(.width(4)) register_1 (.D(adder_1_out), .en(1'b1), .Q(register_1_q), .clk(clock), .clr(and_1_out));
  and and_1 (and_1_out, register_1_q[0], register_1_q[1], register_1_q[2], register_1_q[3]);
  Adder #(.width(4)) adder_1 (.a(num0), .b(register_1_q), .out(adder_1_out), .cin(carry_in), .cout(carry_out));
endmodule

module Ram (
  input  [3:0] Adress_port,
  input  enable_component,
  input  clear__reset_content,
  input  [7:0] datain,
  input  load_memory_to_output,
  output [7:0] outdata
);

  wire not_1_out, not_2_out;
  wire [7:0] data, datain_t;

  RAM #(.addrWidth(4), .bus("asynch")) ram_1 (
    .addr(Adress_port), .data(data), .sel(enable_component), .ld(load_memory_to_output),
    .clr(clear__reset_content));
  not not_1 (not_1_out, load_memory_to_output);
  _4_bit_tri_state_buffer_vanlig u_4_bit_tri_state_buffer_vanlig_1 (
    .in0(datain), .enable0(not_1_out), .in1(data), .enable1(load_memory_to_output), .Out0(data),
    .Out1(datain_t));
  not not_2 (not_2_out, load_memory_to_output);
  _4_bit_2_1_MUX_vanlig u_4_bit_2_1_mux_vanlig_1 (.in0(data), .in1(datain_t), .enable_switch(not_2_out), .out(outdata));

  // Other names for the same wires on the sheet: load = load_memory_to_output

  // Notes on the sheet:
  //   Both in and out port
endmodule

module _4_bit_tri_state_buffer_vanlig (
  input  [7:0] in0,
  input  enable0,
  input  [7:0] in1,
  input  enable1,
  output [7:0] Out0,
  output [7:0] Out1
);

  assign Out0 = enable0 ? in0 : 8'bz;  // Controlled_Buffer controlled_buffer_1
  assign Out1 = enable1 ? in1 : 8'bz;  // Controlled_Buffer controlled_buffer_2
endmodule

module _4_bit_2_1_MUX_vanlig (
  input  [7:0] in0,
  input  [7:0] in1,
  input  enable_switch,
  output [7:0] out
);

  wire not_1_out;

  not not_1 (not_1_out, enable_switch);
  _4_bit_tri_state_buffer_vanlig u_4_bit_tri_state_buffer_vanlig_1 (
    .in0(in0), .enable0(enable_switch), .in1(in1), .enable1(not_1_out), .Out0(out), .Out1(out));
endmodule

module Instruksjonsleser (
  input  [3:0] adress,
  input  [7:0] indata,
  input  in_3,
  input  in_4,
  output [7:0] outdata
);

  wire reset_tunell;

  Ram ram_1 (
    .Adress_port(adress), .datain(indata), .enable_component(in_4), .load_memory_to_output(in_3),
    .clear__reset_content(reset_tunell), .outdata(outdata));
  counter counter_1 (.num0(adress), .clock(in_3), .carry_out(reset_tunell), .carry_in(1'b0));

  // Other names for the same wires on the sheet: adresstunell[3:0] = adress; enable = in_4; loadtunell = in_3
endmodule

module Dataregister_R (
  input  [7:0] indata,
  input  enable,
  input  clear,
  output [7:0] outdata
);

  Register register_1 (.D(indata), .en(1'b1), .Q(outdata), .clk(enable), .clr(clear));
endmodule

module Instruksjonstolker (
  input  [3:0] in_1,
  input  select,
  input  load,
  input  clear,
  output [7:0] out_5
);

  // memory memory_1: pin names not known; wires that end beside it: in_1, select, out_5, clear, load
endmodule

module memory (
  input  [7:0] instruction,
  input  in_2,
  input  in_3,
  input  in_4,
  input  in_5,
  output [3:0] out_6
);


  assign instruction[7:4] = {in_2, in_3, in_4, in_5};
  assign out_6 = instruction[3:0];
endmodule
