// Logisim project first.circ as structural Verilog
module r (
  input  [7:0] in,
  input  enable,
  input  clock,
  input  clear,
  output [7:0] out
);

  Register register_1 (.D(in), .en(enable), .Q(out), .clk(clock), .clr(clear));
endmodule

module get_new_R_from_DDDD (
  input  [7:0] in_R0_R8,
  input  [3:0] D0_D4,
  input  in_3,
  output [7:0] out_R0_R8
);

  wire not_1_out;

  assign out_R0_R8 = not_1_out ? {in_R0_R8[7:4], D0_D4} : 8'bz;  // Controlled_Buffer controlled_buffer_1
  not not_1 (not_1_out, in_3);
  assign out_R0_R8 = in_3 ? {D0_D4, in_R0_R8[3:0]} : 8'bz;  // Controlled_Buffer controlled_buffer_2

  // Other names for the same wires on the sheet: MSB[3:0] = in_R0_R8[7:4]; LSB[3:0] = in_R0_R8[3:0]; Load = in_3
endmodule
