// Logisim project oblig2b.circ as structural Verilog
module counter (
  input  carry_in,
  input  [3:0] num0,
  input  clock,
  output carry_out
);

  wire and_1_out;
  wire [3:0] adder_1_out, register_1_q;

  Register #(.width(4)) register_1 (.D(adder_1_out), .en(1'b1), .Q(register_1_q), .clk(clock), .clr(and_1_out));
  and and_1 (and_1_out, register_1_q[0], register_1_q[1], register_1_q[2], register_1_q[3]);
  Adder #(.width(4)) adder_1 (.a(num0), .b(register_1_q), .out(adder_1_out), .cin(carry_in), .cout(carry_out));
endmodule

module Ram (
  input  [3:0] Adress_port,
  input  enable_component,
  input  clear__reset_content,
  input  [7:0] datain,
  input  load_memory_to_output,
  output [7:0] outdata
);

  wire not_1_out, not_2_out;
  wire [7:0] data, datain_t;

  RAM #(.addrWidth(4), .bus("asynch")) ram_1 (
    .addr(Adress_port), .data(data), .sel(enable_component), .ld(load_memory_to_output),
    .clr(clear__reset_content));
  not not_1 (not_1_out, load_memory_to_output);
  _4_bit_tri_state_buffer_vanlig u_4_bit_tri_state_buffer_vanlig_1 (
    .in0(datain), .enable0(not_1_out), .in1(data), .enable1(load_memory_to_output), .Out0(data),
    .Out1(datain_t));
  not not_2 (not_2_out, load_memory_to_output);
  _4_bit_2_1_MUX_vanlig u_4_bit_2_1_mux_vanlig_1 (.in0(data), .in1(datain_t), .enable_switch(not_2_out), .out(outdata));

  // Other names for the same wires on the sheet: load = load_memory_to_output

  // Notes on the sheet:
  //   Both in and out port
endmodule

module _4_bit_tri_state_buffer_vanlig (
  input  [7:0] in0,
  input  enable0,
  input  [7:0] in1,
  input  enable1,
  output [7:0] Out0,
  output [7:0] Out1
);

  assign Out0 = enable0 ? in0 : 8'bz;  // Controlled_Buffer controlled_buffer_1
  assign Out1 = enable1 ? in1 : 8'bz;  // Controlled_Buffer controlled_buffer_2
endmodule

module _4_bit_2_1_MUX_vanlig (
  input  [7:0] in0,
  input  [7:0] in1,
  input  enable_switch,
  output [7:0] out
);

  wire not_1_out;

  not not_1 (not_1_out, enable_switch);
  _4_bit_tri_state_buffer_vanlig u_4_bit_tri_state_buffer_vanlig_1 (
    .in0(in0), .enable0(enable_switch), .in1(in1), .enable1(not_1_out), .Out0(out), .Out1(out));
endmodule

module Instruksjonsbus (
  input  [3:0] adress,
  input  [7:0] indata,
  input  in_3,
  input  in_4,
  output [7:0] outdata
);

  wire reset_tunell;

  Ram ram_1 (
    .Adress_port(adress), .datain(indata), .enable_component(in_4), .load_memory_to_output(in_3),
    .clear__reset_content(reset_tunell), .outdata(outdata));
  counter counter_1 (.num0(adress), .clock(in_3), .carry_out(reset_tunell), .carry_in(1'b0));

  // Other names for the same wires on the sheet: adresstunell[3:0] = adress; enable = in_4; loadtunell = in_3
endmodule

module Dataregister_R (
  input  [7:0] indata,
  input  enable,
  input  clear,
  output [7:0] outdata
);

  Register register_1 (.D(indata), .en(1'b1), .Q(outdata), .clk(enable), .clr(clear));
endmodule

module instruksjonsleser (
  input  [7:0] instruction,
  output [3:0] adress_data,
  output instr0,
  output instr1,
  output legal
);

  wire and_1_out, xor_1_out;

  and and_1 (and_1_out, 1'b1, instruction[7]);
  xor xor_1 (xor_1_out, instruction[7], instruction[6]);
  and and_2 (legal, and_1_out, xor_1_out);

  assign adress_data = instruction[3:0];
  assign instr0 = instruction[4];
  assign instr1 = instruction[5];
endmodule

module main2 (
  input  [7:0] in_1,
  input  in_2,
  input  in_3,
  input  in_4,
  output legal,
  output instr0,
  output instr1,
  output out_8
);

  wire [3:0] Adress, Data_adress;
  wire [7:0] dataregister_r_1_outdata, indata, instruksjontunell;

  instruksjonsleser instruksjonsleser_1 (
    .instruction(in_1), .legal(legal), .instr1(instr1), .instr0(instr0), .adress_data(Data_adress));
  Dataregister_R dataregister_r_1 (.indata(indata), .enable(in_2), .outdata(dataregister_r_1_outdata), .clear(in_4));
  Instruksjonsbus instruksjonsbus_1 (
    .adress(Adress), .indata(dataregister_r_1_outdata), .in_3(in_3), .outdata(instruksjontunell), .in_4(out_8));
endmodule

module adressconverter (
  input  [3:0] data_adress,
  input  [3:0] original_adress,
  input  instr1,
  input  legal,
  output [3:0] adress
);

  wire and_1_out, not_1_out, not_2_out;

  not not_1 (not_1_out, instr1);
  assign adress = and_1_out ? data_adress : 4'bz;  // Controlled_Buffer controlled_buffer_1
  and and_1 (and_1_out, not_1_out, legal);
  not not_2 (not_2_out, and_1_out);
  assign adress = not_2_out ? original_adress : 4'bz;  // Controlled_Buffer controlled_buffer_2
endmodule

module dataconverter (
  input  instr0,
  input  [3:0] data_adress,
  input  [7:0] original_data,
  input  instr1,
  input  legal,
  output [7:0] data
);

  wire and_1_out, not_1_out;
  wire [7:0] undriven;

  assign data = and_1_out ? undriven : 8'bz;  // Controlled_Buffer controlled_buffer_1
  and and_1 (and_1_out, instr1, legal);
  not not_1 (not_1_out, and_1_out);
  assign data = not_1_out ? original_data : 8'bz;  // Controlled_Buffer controlled_buffer_2

  // Notes on the sheet:
  //   unit for converting the data
endmodule
