// Logisim project second.circ as structural Verilog: 10 circuits, main circuit main
module main (
  input  in_1,
  input  in_2,
  input  in_3,
  input  in_4
);

  wire [3:0] clock_1_adress;
  wire [7:0] ram1_1_data;

  Clock clock_1 (.adress(clock_1_adress), .clear(in_1));
  Ram1 ram1_1 (.adress(clock_1_adress), .data(ram1_1_data));
  instruksjonsbus instruksjonsbus_1 (.instruction(ram1_1_data), .reset_R(in_2), .in_3(in_3), .reset_RAM(in_4));
endmodule

// R
module r (
  input  [7:0] in,
  input  clear,
  output [7:0] out
);

  wire clock_1_out;

  Register register_1 (.D(in), .en(1'b1), .Q(out), .clk(clock_1_out), .clr(clear));
  Clock_part clock_1 (.out(clock_1_out));
endmodule

module instruksjonsbus (
  input  [7:0] instruction,
  input  reset_RAM,
  input  in_3,
  input  reset_R
);

  wire instr0, instr1, legal, nand_1_out;
  wire [3:0] DDDD_AAAA;
  wire [7:0] outData, RData, rincontroller_1_out_7;

  instruksjonsleser instruksjonsleser_1 (
    .in_1(instruction), .DDDD_AAAA(DDDD_AAAA), .instr0(instr0), .instr1(instr1), .legal(legal));
  RIncontroller rincontroller_1 (
    .DDDD_AAAA(DDDD_AAAA), .outData(outData), .instruction(instruction), .instr0(instr0), .instr1(instr1),
    .legal(legal), .out_7(rincontroller_1_out_7));
  r r_1 (.in(rincontroller_1_out_7), .clear(in_3), .out(RData));
  nand nand_1 (nand_1_out, instr1, instr0, legal);
  Ram2 ram2_1 (.Adress(DDDD_AAAA), .indata(RData), .load(nand_1_out), .clear(reset_RAM), .outData(outData));
endmodule

module Rchanger (
  input  [7:0] Rdata,
  input  [3:0] data,
  input  load,
  output [7:0] out_R0_R8
);

  wire not_1_out;

  assign out_R0_R8 = not_1_out ? {Rdata[7:4], data} : 8'bz;  // Controlled_Buffer controlled_buffer_1
  not not_1 (not_1_out, load);
  assign out_R0_R8 = load ? {data, Rdata[3:0]} : 8'bz;  // Controlled_Buffer controlled_buffer_2

  // Other names for the same wires on the sheet: MSB[3:0] = Rdata[7:4]; LSB[3:0] = Rdata[3:0]
endmodule

// instreader
module instruksjonsleser (
  input  [7:0] in_1,
  output [3:0] DDDD_AAAA,
  output instr0,
  output instr1,
  output legal
);

  wire xor_1_out;

  xor xor_1 (xor_1_out, in_1[6], in_1[7]);
  and and_1 (legal, xor_1_out, in_1[7]);

  assign DDDD_AAAA = in_1[3:0];
  assign instr0 = in_1[4];
  assign instr1 = in_1[5];
endmodule

module RIncontroller (
  input  [3:0] DDDD_AAAA,
  input  [7:0] outData,
  input  [7:0] instruction,
  input  instr0,
  input  instr1,
  input  legal,
  output [7:0] out_7
);

  wire and_1_out, and_2_out, not_1_out, not_2_out;
  wire [7:0] n8_bit_tri_state_1_out1, rchanger_1_out_r0_r8;

  not not_1 (not_1_out, instr0);
  and and_1 (and_1_out, legal, not_1_out, instr1);
  not not_2 (not_2_out, instr1);
  Rchanger rchanger_1 (.Rdata(instruction), .data(DDDD_AAAA), .load(instr0), .out_R0_R8(rchanger_1_out_r0_r8));
  _8_bit_tri_state u_8_bit_tri_state_1 (
    .in0(outData), .in1(instruction), .load(and_1_out), .out1(n8_bit_tri_state_1_out1));
  and and_2 (and_2_out, legal, not_2_out);
  _8_bit_tri_state u_8_bit_tri_state_2 (
    .in0(rchanger_1_out_r0_r8), .in1(n8_bit_tri_state_1_out1), .load(and_2_out), .out1(out_7));
endmodule

module _8_bit_tri_state (
  input  [7:0] in0,
  input  [7:0] in1,
  input  load,
  output [7:0] out1
);

  wire not_1_out;

  assign out1 = load ? in0 : 8'bz;  // Controlled_Buffer controlled_buffer_1
  assign out1 = not_1_out ? in1 : 8'bz;  // Controlled_Buffer controlled_buffer_2
  not not_1 (not_1_out, load);
endmodule

module Clock (
  input  clear,
  output [3:0] adress
);

  wire adder_1_cout, clock_1_out, not_1_out;
  wire [3:0] adder_1_out;

  not not_1 (not_1_out, adder_1_cout);
  Clock_part clock_1 (.out(clock_1_out));
  Register #(.width(4)) register_1 (.D(adder_1_out), .en(not_1_out), .Q(adress), .clk(clock_1_out), .clr(clear));
  Adder #(.width(4)) adder_1 (.a(4'b0001), .b(adress), .out(adder_1_out), .cin(1'b0), .cout(adder_1_cout));
endmodule

module Ram1 (
  input  [3:0] adress,
  output [7:0] data
);

  wire clock_1_out;

  Clock_part clock_1 (.out(clock_1_out));
  RAM #(.addrWidth(4)) ram_1 (.addr(adress), .data(data), .sel(1'b1), .clk(clock_1_out), .ld(1'b1), .clr(1'b0));
endmodule

module Ram2 (
  input  [3:0] Adress,
  input  clear,
  input  load,
  input  [7:0] indata,
  output [7:0] outData
);

  wire clock_1_out, not_1_out;

  Clock_part clock_1 (.out(clock_1_out));
  RAM #(.addrWidth(4)) ram_1 (.addr(Adress), .data(outData), .sel(1'b1), .clk(clock_1_out), .ld(load), .clr(clear));
  assign outData = not_1_out ? indata : 8'bz;  // Controlled_Buffer controlled_buffer_1
  not not_1 (not_1_out, load);

  // Other names for the same wires on the sheet: data[7:0] = outData
endmodule
